# Fritzing sketch meteo (saved by Fritzing 0.9.1b)

parts:
  Part1 = Arduino Uno (Rev3)  # not connected
  Part2 = Arduino Ethernet Shield (Rev3)
  LCD1 = LCD screen  # not connected
  RHT1 = Humidity and Temperature Sensor RHT03

nets:
  N1: Part2.GND, RHT1.GND_1
  N2: Part2.PWM_D5, RHT1.Vcc
  N3: Part2.5V, RHT1.Data-signal
